# Fritzing sketch Rangkaian (saved by Fritzing 0.9.3b)
breadboards: 1

parts:
  Mod3 = KY-019 5V Relay Module [package="Breakout board"]
  Mod4 = KY-019 5V Relay Module [package="Breakout board"]
  Mod2 = KY-019 5V Relay Module [package="Breakout board"]
  Mod5 = KY-019 5V Relay Module [package="Breakout board"]
  Mod6 = KY-019 5V Relay Module [package="Breakout board"]
  Mod7 = Amica NodeMCU DevKit 1.0
  Mod8 = KY-015 Temperature & Humidity Sensor Module [package="Breakout board"]
  Part1 = Lilypad Battery Connect
  HLK-PM1 = HLK-PM01

nets:
  N1: Mod3.S, Mod4.S, Mod2.S, Mod5.S, Mod6.-, Mod7.pin1, Mod7.pin_10, Mod7.pin_26, Mod8.S, HLK-PM1.-Vo
  N2: Mod3.+, Mod7.pin6
  N3: Mod3.-, Mod4.-, Mod2.-, Mod5.-, Mod6.S, Mod7.pin2, Mod7.pin_9, Mod7.pin_25, Mod7.pin_29, Mod8.-, HLK-PM1.+Vo
  N4: Mod4.+, Mod7.pin7
  N5: Mod2.+, Mod7.pin4
  N6: Mod2.Common, Part1.+
  N7: Mod5.+, Mod7.pin8
  N8: Mod6.+, Mod7.pin_13
  N9: Mod7.pin_14, Mod8.Vin

custom parts:
  KY-019 5V Relay Module: KY-019 5V Relay module, used to control AC circuits. (Special thanks to vanepp for fixing the PCB holes and other errors)
  Amica NodeMCU DevKit 1.0: Amica NodeMCU DevKit 1.0 Development Kit based on ESP8266 ESP-12E, integating GPIO, PWM, IIC, 1-Wire and ADC all in one board. Links: NodeMCU information page Github
  KY-015 Temperature & Humidity Sensor Module: KY-015 temperature and humidity sensor module, provides a low-latency serial interface to measure humidity and temperature.
